# Fritzing sketch FritzingCircuit (saved by Fritzing 0.8.7b)
breadboards: 1

parts:
  part = Arduino Uno (Rev3) [part_number="Arduino UNO"]
  DHT11 = Humidity and Temperature Sensor RHT03
  LDR = Photocell (LDR) [package=THT]
  R2 = Resistor [tolerance=±5% resistance=10k package=THT]

nets:
  N1: part.A5/SCL, DHT11.Data-signal
  3V3: part.3V3, DHT11.Vcc, LDR.pin_0
  N2: part.GND, DHT11.GND_1, R2.Pin_1
  N3: LDR.pin_1, R2.Pin_0

notes:
  LCD_RD
  LCD_WR
  LCD_RS
  LCD_CS
  LCD_RST
  GND
  5V
  3V3
  LCD_D1
  LCD_D0
  LCD_D7
  LCD_D6
  LCD_D5
  LCD_D4
  LCD_D3
  LCD_D2
  3.5" TFT LCD
